# Fritzing sketch electron (saved by Fritzing 0.9.3b)
breadboards: 1

parts:
  R1 = Resistor [tolerance=±5% resistance=1k package="2010 [SMD]"]
  R2 = PHOTOCELL [package=photocell]
  S1 = Pushbutton [package="[THT]"]
  R3 = Resistor [tolerance=±5% resistance=1k package="2010 [SMD]"]
  LED1 = LEDs [package=led10mm]  # not connected

nets:
  N1: R1.Pin_0, R2.P$2
  N2: R1.Pin_1, R3.Pin_1
  N3: R2.P$1, S1.Pin_3, S1.Pin_4
  N4: S1.Pin_1, S1.Pin_2, R3.Pin_0
