# Fritzing sketch tessel (saved by Fritzing 0.9.3b)
breadboards: 1

parts:
  R1 = PHOTOCELL [package=photocell]
  R2 = Resistor [tolerance=±5% resistance=10k package="0402 [SMD]"]
  S1 = Pushbutton [package="[THT]"]
  R3 = Resistor [tolerance=±5% resistance=10k package="0402 [SMD]"]
  LED1 = LEDs [package=led10mm]

nets:
  N1: R1.P$1, S1.Pin_1, S1.Pin_2
  N2: R1.P$2, R2.Pin_0
  N3: R2.Pin_1, R3.Pin_1, LED1.A
  N4: S1.Pin_3, S1.Pin_4, R3.Pin_0
